# Fritzing sketch arm schematic (saved by Fritzing 0.9.3b)
breadboards: 1

parts:
  Part1 = Arduino Nano (Rev3.0)
  Part2 = MicroSD Card Module
  S1 = Momentary Switch [package=ksa_sealed_tac_switch]
  S2 = Momentary Switch [package=ksa_sealed_tac_switch]
  S3 = Momentary Switch [package=ksa_sealed_tac_switch]
  R1 = Resistor [tolerance=±5% resistance=220 package=THT]
  R2 = Resistor [tolerance=±5% resistance=220 package=THT]
  R3 = Resistor [tolerance=±5% resistance=220 package=THT]
  LED1 = LED - 5mm [color="Red (633nm)" package="5 mm [THT]"]
  LED2 = LED - 5mm [color="Red (633nm)" package="5 mm [THT]"]
  LED3 = LED - 5mm [color="Red (633nm)" package="5 mm [THT]"]
  LED4 = LED - 5mm [color="Red (633nm)" package="5 mm [THT]"]
  R4 = Resistor [tolerance=±5% resistance=220 package=THT]
  R5 = Resistor [tolerance=±5% resistance=220 package=THT]
  R6 = Resistor [tolerance=±5% resistance=220 package=THT]
  R7 = Resistor [tolerance=±5% resistance=220 package=THT]
  R8 = Rotary Potentiometer (Small) [maximum_resistance=100kΩ package=THT]
  R9 = Rotary Potentiometer (Small) [maximum_resistance=100kΩ package=THT]
  R10 = Rotary Potentiometer (Small) [maximum_resistance=100kΩ package=THT]
  R11 = Rotary Potentiometer (Small) [maximum_resistance=100kΩ package=THT]
  PWM1 = PCA9685 16x12-bit PWM Breakout
  J1 = Basic Servo
  J2 = Power Jack [package=power_jack_smd]

nets:
  GND: Part1.GND, Part2.GND, R1.Pin_1, R2.Pin_1, R3.Pin_1, R4.Pin_1, R7.Pin_1, R8.leg1, R9.leg1, R10.leg1, R11.leg1, PWM1.no_name_yet#501, PWM1.no_name_yet#701, PWM1.no_name_yet#1000, J2.GND
  N1: Part1.D3, LED1.cathode
  N2: Part1.D4, LED2.cathode
  N3: Part1.D5, S1.1
  N4: Part1.D6, LED3.cathode
  N5: Part1.D7, LED4.cathode
  N6: Part1.D8, S2.1
  N7: Part1.D9, S3.1
  N8: Part1.D10, Part2.CS
  N9: Part1.D11/MOSI, Part2.MOSI
  N10: Part1.D12/MISO, Part2.MISO
  N11: Part1.VIN, PWM1.no_name_yet#100, PWM1.no_name_yet#706, J2.GNDBREAK
  5V: Part1.5V, Part2.VCC, S1.4, S2.4, S3.4, R8.leg2, R9.leg2, R10.leg2, R11.leg2, PWM1.no_name_yet#505
  N12: Part1.A5, PWM1.no_name_yet#504
  N13: Part1.A4, PWM1.no_name_yet#503
  N14: Part1.A3, R11.wiper
  N15: Part1.A2, R10.wiper
  N16: Part1.A1, R9.wiper
  N17: Part1.A0, R8.wiper
  N18: Part1.D13/SCK, Part2.SCK
  N19: S1.2, R1.Pin_0
  N20: S2.2, R2.Pin_0
  N21: S3.2, R3.Pin_0
  N22: LED1.anode, R4.Pin_0
  N23: LED2.anode, R5.Pin_0
  N24: LED3.anode, R6.Pin_0
  N25: LED4.anode, R7.Pin_0
  N26: PWM1.no_name_yet#0, J1.pulse

notes:
  cs sck mosi miso vcc gnd
